// Logisim project decompress.circ as structural Verilog: 4 circuits, main circuit Multiplier
module Multiplier (
  input  [7:0] A,
  input  RESET,
  input  [7:0] B,
  output DONE,
  output [15:0] PRODUCT
);

  wire and_1_out, and_2_out, clock_1_out, clock_2_out, inmultiplier_1_to_add_or_not, not_1_out, not_2_out,
       or_1_out;
  wire [7:0] inmultiplier_1_out_7;
  wire [15:0] inmulitplicand_1_out_6, multiplexer_1_out;

  and and_1 (and_1_out, not_1_out, clock_1_out);
  not not_1 (not_1_out, RESET);
  Clock clock_1 (.out(clock_1_out));
  // Probe on A
  Clock clock_2 (.out(clock_2_out));
  and and_2 (and_2_out, and_1_out, not_2_out);
  not not_2 (not_2_out, DONE);
  // Probe on B
  inmultiplier inmultiplier_1 (
    .A(A), .Load(RESET), .Shift(1'b1), .clock(clock_2_out), .to_add_or_not(inmultiplier_1_to_add_or_not),
    .out_7(inmultiplier_1_out_7));  // open: Reset
  // Probe on inmultiplier_1_out_7
  Counter #(.width(3), .max('h7), .ongoal("stay")) Counter (
    .D(3'b000), .count(1'b1), .carry(DONE), .clk(and_2_out), .clr(RESET));  // open: load, Q
  inmulitplicand inmulitplicand_1 (
    .B(B), .Load(RESET), .Shift(1'b1), .clock(clock_2_out), .out_6(inmulitplicand_1_out_6));  // open: Reset
  // Probe on inmulitplicand_1_out_6
  Multiplexer #(.width(16), .disabled(0)) multiplexer_1 (
    .in1(inmulitplicand_1_out_6), .out(multiplexer_1_out), .sel(or_1_out), .en(inmultiplier_1_to_add_or_not));  // open: in0
  addingstuff addingstuff_1 (
    .to_be_added(multiplexer_1_out), .current_total(PRODUCT), .reset(RESET), .clock(or_1_out), .out_5(PRODUCT));
  or or_1 (or_1_out, clock_2_out, RESET);
  // Probe on PRODUCT

  // Notes on the sheet:
  //   Alexander Chatron-Michaud, 260611509
  //   This circuit loads the values when the reset button is on and begins multiplying when reset is turned off
endmodule

module inmultiplier (
  input  [7:0] A,
  input  Load,
  input  Shift,
  input  Reset,
  input  clock,
  output to_add_or_not,
  output [7:0] out_7
);

  Shift_Register shift_register_1 (
    .shift(Shift), .in(1'b0), .clk(clock), .out(to_add_or_not), .load(Load), .clr(Reset), .d0(A[7]),
    .q0(out_7[7]), .d1(A[6]), .q1(out_7[6]), .d2(A[5]), .q2(out_7[5]), .d3(A[4]), .q3(out_7[4]), .d4(A[3]),
    .q4(out_7[3]), .d5(A[2]), .q5(out_7[2]), .d6(A[1]), .q6(out_7[1]), .d7(A[0]), .q7(out_7[0]));
endmodule

module addingstuff (
  input  [15:0] to_be_added,
  input  [15:0] current_total,
  input  clock,
  input  reset,
  output [15:0] out_5
);

  wire adder_1_cout, register_1_q;
  wire [15:0] adder_1_out, register_2_q;

  // Probe on register_2_q
  Adder #(.width(16)) adder_1 (
    .a(to_be_added), .b(register_2_q), .out(adder_1_out), .cin(register_1_q), .cout(adder_1_cout));
  Register #(.width(1)) register_1 (.D(adder_1_cout), .Q(register_1_q), .clk(clock), .clr(clock));  // open: en
  Multiplexer #(.width(16), .disabled(0), .enable("false")) multiplexer_1 (
    .in0(register_2_q), .in1(adder_1_out), .out(out_5), .sel(clock));
  Register #(.width(16), .trigger("falling")) register_2 (
    .D(out_5), .Q(register_2_q), .clk(clock), .clr(reset));  // open: en
endmodule

module inmulitplicand (
  input  [7:0] B,
  input  Load,
  input  Shift,
  input  Reset,
  input  clock,
  output [15:0] out_6
);

  wire [15:0] bit_extender_1_out;

  assign bit_extender_1_out = {{8{1'b0}}, B};  // Bit_Extender bit_extender_1
  Shift_Register #(.length(16)) shift_register_1 (
    .shift(Shift), .in(1'b0), .clk(clock), .load(Load), .clr(Reset), .d0(bit_extender_1_out[0]),
    .q0(out_6[0]), .d1(bit_extender_1_out[1]), .q1(out_6[1]), .d2(bit_extender_1_out[2]), .q2(out_6[2]),
    .d3(bit_extender_1_out[3]), .q3(out_6[3]), .d4(bit_extender_1_out[4]), .q4(out_6[4]),
    .d5(bit_extender_1_out[5]), .q5(out_6[5]), .d6(bit_extender_1_out[6]), .q6(out_6[6]),
    .d7(bit_extender_1_out[7]), .q7(out_6[7]), .d8(bit_extender_1_out[8]), .q8(out_6[8]),
    .d9(bit_extender_1_out[9]), .q9(out_6[9]), .d10(bit_extender_1_out[10]), .q10(out_6[10]),
    .d11(bit_extender_1_out[11]), .q11(out_6[11]), .d12(bit_extender_1_out[12]), .q12(out_6[12]),
    .d13(bit_extender_1_out[13]), .q13(out_6[13]), .d14(bit_extender_1_out[14]), .q14(out_6[14]),
    .d15(bit_extender_1_out[15]), .q15(out_6[15]));  // open: out
endmodule
